# Fritzing sketch chicken-safe (saved by Fritzing 0.9.3b)
breadboards: 1

parts:
  Composant1 = Arduino Nano (Rev3.0)
  Composant2 = Real Time Clock Module - DS1307 RTC Breakout Board
  WeMos_D1_Mini_OLED_Shield1 = WeMos D1 Mini OLED Shield  # not connected

nets:
  5V: Composant1.5V, Composant2.5V
